# Fritzing sketch schematic (saved by Fritzing 0.9.3b)

parts:
  Stepper_Motor = Stepper Motor - Bipolar
  Stepper_Driver = Pololu A4988 [package=SO16]
  enable = female pin header, 2 pins [form="♀ (female)"]
  12V = Screw terminal - 2 pins [package=THT]
  Arduino = Arduino Board Ethernet

nets:
  N1: Stepper_Motor.A, Stepper_Driver.2B
  N2: Stepper_Motor.C, Stepper_Driver.2A
  N3: Stepper_Motor.B, Stepper_Driver.1A
  N4: Stepper_Motor.D, Stepper_Driver.1B
  N5: Stepper_Driver.RESET, enable.pin2
  N6: Stepper_Driver.SLEEP, enable.pin1
  N7: Stepper_Driver.STEP, Arduino.D3_PWM
  N8: Stepper_Driver.DIR, Arduino.D4
  N9: Stepper_Driver.GND#8, Arduino.GND
  VDD: Stepper_Driver.VDD, Arduino.5V
  N10: Stepper_Driver.GND#14, 12V.pin2
  N11: Stepper_Driver.VMOT, 12V.pin1
